// Logisim project Ninja_project.circ as structural Verilog: 6 circuits, main circuit main
module main (
  input  set
);

  wire _0_out, _1_out, _2_out, _3_out, _4_out, _5_out, _6_out, _7_out, _8_out, _9_out, comparator_1_output,
       encoder_a, encoder_b, encoder_c, encoder_d, encoder_enable, n7_segment_1_a_2, n7_segment_1_b_2,
       n7_segment_1_c_2, n7_segment_1_d_2, n7_segment_1_e, n7_segment_1_f, n7_segment_1_g, output_1_a_2,
       output_1_b, output_1_c, output_1_d, output_1_e, output_1_f, Reset_input_out, Reset_Pass_out;
  wire [3:0] resistor_1_x0, resistor_1_x1, resistor_1_x2, resistor_1_x3, resistor_1_x4, resistor_1_y0,
       resistor_1_y1, resistor_1_y2, resistor_1_y3, resistor_1_y4;

  Button _0 (.out(_0_out));
  Button _1 (.out(_1_out));
  Button _2 (.out(_2_out));
  Button _3 (.out(_3_out));
  Button _4 (.out(_4_out));
  Button _5 (.out(_5_out));
  Button _6 (.out(_6_out));
  Button _7 (.out(_7_out));
  Button _8 (.out(_8_out));
  Button _9 (.out(_9_out));
  Button Reset_Pass (.out(Reset_Pass_out));
  Button Reset_input (.out(Reset_input_out));
  DCML_to_BCD encoder (
    ._0(_0_out), ._1(_1_out), ._2(_2_out), ._3(_3_out), ._4(_4_out), ._5(_5_out), ._6(_6_out), ._7(_7_out),
    ._8(_8_out), ._9(_9_out), .Enable(encoder_enable), .A(encoder_a), .B(encoder_b), .C(encoder_c),
    .D(encoder_d));
  resistor resistor_1 (
    .in_1(encoder_a), .in_2(encoder_b), .in_3(encoder_c), .in_4(encoder_d), .rsi(Reset_input_out),
    .rsp(Reset_Pass_out), .E(encoder_enable), .Sp(set), .x4(resistor_1_x4), .y4(resistor_1_y4),
    .x3(resistor_1_x3), .y3(resistor_1_y3), .x2(resistor_1_x2), .y2(resistor_1_y2), .x1(resistor_1_x1),
    .y1(resistor_1_y1), .x0(resistor_1_x0), .y0(resistor_1_y0));
  comparator comparator_1 (
    .A4(resistor_1_x4), .B4(resistor_1_y4), .A3(resistor_1_x3), .B3(resistor_1_y3), .A2(resistor_1_x2),
    .B2(resistor_1_y2), .A1(resistor_1_x1), .B1(resistor_1_y1), .X1(resistor_1_x0), .X2(resistor_1_y0),
    .\output (comparator_1_output));
  _7_Segment u_7_segment_1 (
    .A(encoder_a), .B(encoder_b), .C(encoder_c), .D(encoder_d), .En(encoder_enable), .A_2(n7_segment_1_a_2),
    .B_2(n7_segment_1_b_2), .C_2(n7_segment_1_c_2), .D_2(n7_segment_1_d_2), .E(n7_segment_1_e),
    .F(n7_segment_1_f), .G(n7_segment_1_g));
  \output  output_1 (
    .A(comparator_1_output), .e(output_1_e), .a_2(output_1_a_2), .b(output_1_b), .c(output_1_c),
    .d(output_1_d), .f(output_1_f));
  _7_Segment_Display u_7_segment_display_1 (
    .g(n7_segment_1_g), .f(n7_segment_1_f), .a(n7_segment_1_a_2), .b(n7_segment_1_b_2), .e(n7_segment_1_e),
    .d(n7_segment_1_d_2), .c(n7_segment_1_c_2));  // open: dp
  _7_Segment_Display u_7_segment_display_2 (
    .f(output_1_a_2), .a(output_1_b), .b(output_1_c), .e(output_1_d), .d(output_1_e), .c(output_1_f));  // open: g, dp
endmodule

// D_TO_BCD
module DCML_to_BCD (
  input  _0,
  input  _1,
  input  _2,
  input  _3,
  input  _4,
  input  _5,
  input  _6,
  input  _7,
  input  _8,
  input  _9,
  output Enable,
  output A,
  output B,
  output C,
  output D
);

  wire and_1_out, and_2_out, and_3_out, and_4_out, and_5_out, and_6_out, and_7_out, and_8_out, and_9_out;

  or or_1 (Enable, _0, _1, _2, _3, _4, _5, _6, _7, _8, _9);
  and and_1 (and_1_out, _3, Enable);
  and and_2 (and_2_out, _4, Enable);
  and and_3 (and_3_out, _5, Enable);
  and and_4 (and_4_out, _6, Enable);
  and and_5 (and_5_out, _7, Enable);
  and and_6 (and_6_out, _8, Enable);
  and and_7 (and_7_out, _9, Enable);
  and and_8 (and_8_out, _1, Enable);
  and and_9 (and_9_out, _2, Enable);
  or u_A (A, and_6_out, and_7_out);
  or u_B (B, and_5_out, and_2_out, and_3_out, and_4_out);
  or u_C (C, and_9_out, and_1_out, and_4_out, and_5_out);
  or u_D (D, and_8_out, and_1_out, and_3_out, and_5_out, and_7_out);
endmodule

// 7_segment_Input
module _7_Segment (
  input  A,
  input  B,
  input  C,
  input  D,
  input  En,
  output A_2,
  output B_2,
  output C_2,
  output D_2,
  output E,
  output F,
  output G
);

  wire B_prime_C_out, B_prime_D_prime_out, BC_prime_D_out, BC_prime_out, BD_out, BD_prime_out,
       C_prime_D_prime_out, CD_out, CD_prime_out, not_1_out, not_2_out, not_3_out, or_1_out, or_2_out,
       or_3_out, or_4_out, or_5_out, or_6_out, or_7_out;

  not not_1 (not_1_out, B);
  not not_2 (not_2_out, C);
  not not_3 (not_3_out, D);
  and CD_prime (CD_prime_out, C, not_3_out);
  and B_prime_C (B_prime_C_out, not_1_out, C);
  and BC_prime (BC_prime_out, B, not_2_out);
  and BD_prime (BD_prime_out, B, not_3_out);
  and BD (BD_out, B, D);
  and B_prime_D_prime (B_prime_D_prime_out, not_1_out, not_3_out);
  and CD (CD_out, C, D);
  and C_prime_D_prime (C_prime_D_prime_out, not_2_out, not_3_out);
  or or_1 (or_1_out, B, not_2_out, D);
  and BC_prime_D (BC_prime_D_out, D, BC_prime_out);
  or or_2 (or_2_out, CD_out, not_1_out, C_prime_D_prime_out);
  or or_3 (or_3_out, B_prime_D_prime_out, CD_prime_out, B_prime_C_out, A, BC_prime_D_out);
  or or_4 (or_4_out, C_prime_D_prime_out, BD_prime_out, BC_prime_out, A);
  or or_5 (or_5_out, CD_prime_out, BC_prime_out, A, B_prime_C_out);
  or or_6 (or_6_out, BD_out, B_prime_D_prime_out, A, C);
  or or_7 (or_7_out, CD_prime_out, B_prime_D_prime_out);
  and and_1 (A_2, or_6_out, En);
  and and_2 (B_2, or_2_out, En);
  and and_3 (C_2, En, or_1_out);
  and and_4 (D_2, or_3_out, En);
  and and_5 (E, or_7_out, En);
  and and_6 (F, or_4_out, En);
  and and_7 (G, or_5_out, En);
endmodule

module \output  (
  input  A,
  output e,
  output a_2,
  output b,
  output c,
  output d,
  output f
);

  wire not_1_out;

  not not_1 (not_1_out, A);
  or or_1 (a_2, not_1_out, A);

  assign b = a_2;
  assign c = a_2;
  assign d = a_2;
  assign e = A;
  assign f = a_2;
endmodule

module comparator (
  input  [3:0] A4,
  input  [3:0] B4,
  input  [3:0] A3,
  input  [3:0] B3,
  input  [3:0] A2,
  input  [3:0] B2,
  input  [3:0] A1,
  input  [3:0] B1,
  input  [3:0] X1,
  input  [3:0] X2,
  output \output 
);

  wire comparator_1_eq, comparator_2_eq, comparator_3_eq, comparator_4_eq, comparator_5_eq;

  Comparator #(.width(4)) comparator_1 (.a(A4), .b(B4), .eq(comparator_1_eq));  // open: gt, lt
  Comparator #(.width(4)) comparator_2 (.a(A3), .b(B3), .eq(comparator_2_eq));  // open: gt, lt
  Comparator #(.width(4)) comparator_3 (.a(A2), .b(B2), .eq(comparator_3_eq));  // open: gt, lt
  Comparator #(.width(4)) comparator_4 (.a(A1), .b(B1), .eq(comparator_4_eq));  // open: gt, lt
  Comparator #(.width(4)) comparator_5 (.a(X1), .b(X2), .eq(comparator_5_eq));  // open: gt, lt
  and and_1 (\output , comparator_1_eq, comparator_2_eq, comparator_3_eq, comparator_4_eq, comparator_5_eq);

  // Notes on the sheet:
  //   P
  //   Q
  //   R
  //   S
endmodule

module resistor (
  input  in_1,
  input  in_2,
  input  in_3,
  input  in_4,
  input  rsi,
  input  rsp,
  input  E,
  input  Sp,
  output [3:0] x4,
  output [3:0] y4,
  output [3:0] x3,
  output [3:0] y3,
  output [3:0] x2,
  output [3:0] y2,
  output [3:0] x1,
  output [3:0] y1,
  output [3:0] x0,
  output [3:0] y0
);

  wire demultiplexer_1_out0, demultiplexer_1_out1;

  Demultiplexer demultiplexer_1 (
    .out0(demultiplexer_1_out0), .out1(demultiplexer_1_out1), .in(E), .sel(Sp));  // open: en
  Register #(.width(4)) register_1 (
    .D({in_4, in_3, in_2, in_1}), .Q(x4), .clk(demultiplexer_1_out0), .clr(rsi));  // open: en
  Register #(.width(4)) register_2 (
    .D({in_4, in_3, in_2, in_1}), .Q(y4), .clk(demultiplexer_1_out1), .clr(rsp));  // open: en
  Register #(.width(4)) register_3 (.D(x4), .Q(x3), .clk(demultiplexer_1_out0), .clr(rsi));  // open: en
  Register #(.width(4)) register_4 (.D(y4), .Q(y3), .clk(demultiplexer_1_out1), .clr(rsp));  // open: en
  Register #(.width(4)) register_5 (.D(x3), .Q(x2), .clk(demultiplexer_1_out0), .clr(rsi));  // open: en
  Register #(.width(4)) register_6 (.D(y3), .Q(y2), .clk(demultiplexer_1_out1), .clr(rsp));  // open: en
  Register #(.width(4)) register_7 (.D(x2), .Q(x1), .clk(demultiplexer_1_out0), .clr(rsi));  // open: en
  Register #(.width(4)) register_8 (.D(y1), .Q(y0), .clk(demultiplexer_1_out1), .clr(rsp));  // open: en
  Register #(.width(4)) register_9 (.D(y2), .Q(y1), .clk(demultiplexer_1_out1), .clr(rsp));  // open: en
  Register #(.width(4)) register_10 (.D(x1), .Q(x0), .clk(demultiplexer_1_out0), .clr(rsi));  // open: en
endmodule
