// Logisim project ninja_with_shift2.circ as structural Verilog: 7 circuits, main circuit main
module main (
  input  s1,
  input  s2,
  input  s3
);

  wire _0_out, _1_out, _2_out, _3_out, _4_out, _5_out, _6_out, _7_out, _8_out, _9_out, a1, a2, a3, a4, a5,
       a6, a7, b1, b2, b3, b4, b5, b6, b7, c1, c2, c3, c4, c5, c6, c7, comparator_1_output,
       comparator_2_output, comparator_3_output, control_1_i, control_1_p1, control_1_p2, control_1_p3, d1,
       d2, d3, d4, d5, d6, d7, e1, e2, e3, e4, e5, e6, e7, encoder_enable, f1, f2, f3, f4, f5, f6, f7, g1,
       g2, g3, g4, g5, g6, g7, h1, h2, h3, h4, h5, h6, h7, i1, i2, i3, i4, i5, i6, i7, j1, j2, j3, j4, j5,
       j6, j7, k1, k2, k3, k4, k5, k6, k7, l1, l2, l3, l4, l5, l6, l7, m1, m2, m3, m4, m5, m6, m7, n1, n2,
       n3, n4, n5, n6, n7, n7_segment_1_a_2, n7_segment_1_b_2, n7_segment_1_c_2, n7_segment_1_d_2,
       n7_segment_1_e, n7_segment_1_f, n7_segment_1_g, o1, o2, o3, o4, o5, o6, o7, or_1_out, output_1_a_2,
       output_1_b, output_1_c, output_1_d, output_1_e, output_1_f, Reset_input_out, Rst_pass1_out,
       Rst_pass2_out, Rst_pass3_out;
  wire [3:0] Check_pass_q0, Check_pass_q1, Check_pass_q2, Check_pass_q3, Check_pass_q4, encoder_d,
       Store_memory1_q0, Store_memory1_q1, Store_memory1_q2, Store_memory1_q3, Store_memory1_q4,
       store_memory2_q0, store_memory2_q1, store_memory2_q2, store_memory2_q3, store_memory2_q4,
       store_memory3_q0, store_memory3_q1, store_memory3_q2, store_memory3_q3, store_memory3_q4;

  Button _0 (.out(_0_out));
  Button _1 (.out(_1_out));
  Button _2 (.out(_2_out));
  Button _3 (.out(_3_out));
  Button _4 (.out(_4_out));
  Button _5 (.out(_5_out));
  Button _6 (.out(_6_out));
  Button _7 (.out(_7_out));
  Button _8 (.out(_8_out));
  Button _9 (.out(_9_out));
  Button Rst_pass3 (.out(Rst_pass3_out));
  Button Reset_input (.out(Reset_input_out));
  Button Rst_pass1 (.out(Rst_pass1_out));
  Button Rst_pass2 (.out(Rst_pass2_out));
  DCML_to_BCD encoder (
    ._0(_0_out), ._1(_1_out), ._2(_2_out), ._3(_3_out), ._4(_4_out), ._5(_5_out), ._6(_6_out), ._7(_7_out),
    ._8(_8_out), ._9(_9_out), .Enable(encoder_enable), .A(encoder_d[3]), .B(encoder_d[2]), .C(encoder_d[1]),
    .D(encoder_d[0]));
  control control_1 (
    .e(encoder_enable), .s1(s1), .s2(s2), .s3(s3), .I(control_1_i), .p1(control_1_p1), .p2(control_1_p2),
    .p3(control_1_p3));
  Shift_Register #(.width(4), .length(5), .trigger("falling")) Check_pass (
    .shift(control_1_i), .in(encoder_d), .clk(encoder_enable), .clr(Reset_input_out), .q0(Check_pass_q0),
    .q1(Check_pass_q1), .q2(Check_pass_q2), .q3(Check_pass_q3), .q4(Check_pass_q4));  // open: out, load, d0, d1, d2, d3, d4
  comparator comparator_1 (
    .A4(Check_pass_q4), .B4(Store_memory1_q4), .A3(Check_pass_q3), .B3(Store_memory1_q3), .A2(Check_pass_q2),
    .B2(Store_memory1_q2), .A1(Check_pass_q1), .B1(Store_memory1_q1), .X1(Check_pass_q0),
    .X2(Store_memory1_q0), .\output (comparator_1_output));
  _7_Segment u_7_segment_1 (
    .A(encoder_d[3]), .B(encoder_d[2]), .C(encoder_d[1]), .D(encoder_d[0]), .En(encoder_enable),
    .A_2(n7_segment_1_a_2), .B_2(n7_segment_1_b_2), .C_2(n7_segment_1_c_2), .D_2(n7_segment_1_d_2),
    .E(n7_segment_1_e), .F(n7_segment_1_f), .G(n7_segment_1_g));
  Shift_Register #(.width(4), .length(5), .trigger("falling")) Store_memory1 (
    .shift(control_1_p1), .in(encoder_d), .clk(encoder_enable), .clr(Rst_pass1_out), .q0(Store_memory1_q0),
    .q1(Store_memory1_q1), .q2(Store_memory1_q2), .q3(Store_memory1_q3), .q4(Store_memory1_q4));  // open: out, load, d0, d1, d2, d3, d4
  _7_Segment_Display u_7_segment_display_1 (
    .g(n7_segment_1_g), .f(n7_segment_1_f), .a(n7_segment_1_a_2), .b(n7_segment_1_b_2), .e(n7_segment_1_e),
    .d(n7_segment_1_d_2), .c(n7_segment_1_c_2));  // open: dp
  comparator comparator_2 (
    .A4(Check_pass_q4), .B4(store_memory2_q0), .A3(Check_pass_q3), .B3(store_memory2_q1), .A2(Check_pass_q2),
    .B2(store_memory2_q2), .A1(Check_pass_q1), .B1(store_memory2_q3), .X1(Check_pass_q0),
    .X2(store_memory2_q4), .\output (comparator_2_output));
  Shift_Register #(.width(4), .length(5), .trigger("falling")) store_memory2 (
    .shift(control_1_p2), .in(encoder_d), .clk(encoder_enable), .clr(Rst_pass2_out), .q0(store_memory2_q0),
    .q1(store_memory2_q1), .q2(store_memory2_q2), .q3(store_memory2_q3), .q4(store_memory2_q4));  // open: out, load, d0, d1, d2, d3, d4
  Shift_Register #(.width(4), .length(5), .trigger("falling")) store_memory3 (
    .shift(control_1_p3), .in(encoder_d), .clk(encoder_enable), .clr(Rst_pass3_out), .q0(store_memory3_q0),
    .q1(store_memory3_q1), .q2(store_memory3_q2), .q3(store_memory3_q3), .q4(store_memory3_q4));  // open: out, load, d0, d1, d2, d3, d4
  comparator comparator_3 (
    .A4(Check_pass_q4), .B4(store_memory3_q0), .A3(Check_pass_q3), .B3(store_memory3_q1), .A2(Check_pass_q2),
    .B2(store_memory3_q2), .A1(Check_pass_q1), .B1(store_memory3_q3), .X1(Check_pass_q0),
    .X2(store_memory3_q4), .\output (comparator_3_output));
  display display_1 (
    .A(store_memory3_q4[3]), .B(store_memory3_q4[2]), .C(store_memory3_q4[1]), .D(store_memory3_q4[0]),
    .A_2(k1), .B_2(k2), .C_2(k3), .D_2(k4), .E(k5), .F(k6), .G(k7));
  display display_2 (
    .A(store_memory3_q3[3]), .B(store_memory3_q3[2]), .C(store_memory3_q3[1]), .D(store_memory3_q3[0]),
    .A_2(l1), .B_2(l2), .C_2(l3), .D_2(l4), .E(l5), .F(l6), .G(l7));
  or or_1 (or_1_out, comparator_3_output, comparator_1_output, comparator_2_output);
  _7_Segment_Display u_7_segment_display_2 (.g(a7), .f(a6), .a(a1), .b(a2), .e(a5), .d(a4), .c(a3));  // open: dp
  display display_3 (
    .A(store_memory2_q4[3]), .B(store_memory2_q4[2]), .C(store_memory2_q4[1]), .D(store_memory2_q4[0]),
    .A_2(f1), .B_2(f2), .C_2(f3), .D_2(f4), .E(f5), .F(f6), .G(f7));
  display display_4 (
    .A(store_memory2_q3[3]), .B(store_memory2_q3[2]), .C(store_memory2_q3[1]), .D(store_memory2_q3[0]),
    .A_2(g1), .B_2(g2), .C_2(g3), .D_2(g4), .E(g5), .F(g6), .G(g7));
  _7_Segment_Display u_7_segment_display_3 (.g(k7), .f(k6), .a(k1), .b(k2), .e(k5), .d(k4), .c(k3));  // open: dp
  \output  output_1 (
    .A(or_1_out), .e(output_1_e), .a_2(output_1_a_2), .b(output_1_b), .c(output_1_c), .d(output_1_d),
    .f(output_1_f));
  _7_Segment_Display u_7_segment_display_4 (.g(c7), .f(c6), .a(c1), .b(c2), .e(c5), .d(c4), .c(c3));  // open: dp
  _7_Segment_Display u_7_segment_display_5 (.g(b7), .f(b6), .a(b1), .b(b2), .e(b5), .d(b4), .c(b3));  // open: dp
  display display_5 (
    .A(Store_memory1_q4[3]), .B(Store_memory1_q4[2]), .C(Store_memory1_q4[1]), .D(Store_memory1_q4[0]),
    .A_2(a1), .B_2(a2), .C_2(a3), .D_2(a4), .E(a5), .F(a6), .G(a7));
  _7_Segment_Display u_7_segment_display_6 (.g(g7), .f(g6), .a(g1), .b(g2), .e(g5), .d(g4), .c(g3));  // open: dp
  _7_Segment_Display u_7_segment_display_7 (.g(f7), .f(f6), .a(f1), .b(f2), .e(f5), .d(f4), .c(f3));  // open: dp
  _7_Segment_Display u_7_segment_display_8 (.g(m7), .f(m6), .a(m1), .b(m2), .e(m5), .d(m4), .c(m3));  // open: dp
  _7_Segment_Display u_7_segment_display_9 (.g(l7), .f(l6), .a(l1), .b(l2), .e(l5), .d(l4), .c(l3));  // open: dp
  _7_Segment_Display u_7_segment_display_10 (
    .f(output_1_a_2), .a(output_1_b), .b(output_1_c), .e(output_1_d), .d(output_1_e), .c(output_1_f));  // open: g, dp
  _7_Segment_Display u_7_segment_display_11 (.g(e7), .f(e6), .a(e1), .b(e2), .e(e5), .d(e4), .c(e3));  // open: dp
  _7_Segment_Display u_7_segment_display_12 (.g(d7), .f(d6), .a(d1), .b(d2), .e(d5), .d(d4), .c(d3));  // open: dp
  _7_Segment_Display u_7_segment_display_13 (.g(i7), .f(i6), .a(i1), .b(i2), .e(i5), .d(i4), .c(i3));  // open: dp
  _7_Segment_Display u_7_segment_display_14 (.g(h7), .f(h6), .a(h1), .b(h2), .e(h5), .d(h4), .c(h3));  // open: dp
  _7_Segment_Display u_7_segment_display_15 (.g(o7), .f(o6), .a(o1), .b(o2), .e(o5), .d(o4), .c(o3));  // open: dp
  _7_Segment_Display u_7_segment_display_16 (.g(n7), .f(n6), .a(n1), .b(n2), .e(n5), .d(n4), .c(n3));  // open: dp
  display display_6 (
    .A(Store_memory1_q3[3]), .B(Store_memory1_q3[2]), .C(Store_memory1_q3[1]), .D(Store_memory1_q3[0]),
    .A_2(b1), .B_2(b2), .C_2(b3), .D_2(b4), .E(b5), .F(b6), .G(b7));
  _7_Segment_Display u_7_segment_display_17 (.g(j7), .f(j6), .a(j1), .b(j2), .e(j5), .d(j4), .c(j3));  // open: dp
  display display_7 (
    .A(Store_memory1_q0[3]), .B(Store_memory1_q0[2]), .C(Store_memory1_q0[1]), .D(Store_memory1_q0[0]),
    .A_2(e1), .B_2(e2), .C_2(e3), .D_2(e4), .E(e5), .F(e6), .G(e7));
  display display_8 (
    .A(Store_memory1_q2[3]), .B(Store_memory1_q2[2]), .C(Store_memory1_q2[1]), .D(Store_memory1_q2[0]),
    .A_2(c1), .B_2(c2), .C_2(c3), .D_2(c4), .E(c5), .F(c6), .G(c7));
  display display_9 (
    .A(store_memory2_q2[3]), .B(store_memory2_q2[2]), .C(store_memory2_q2[1]), .D(store_memory2_q2[0]),
    .A_2(h1), .B_2(h2), .C_2(h3), .D_2(h4), .E(h5), .F(h6), .G(h7));
  display display_10 (
    .A(store_memory2_q1[3]), .B(store_memory2_q1[2]), .C(store_memory2_q1[1]), .D(store_memory2_q1[0]),
    .A_2(i1), .B_2(i2), .C_2(i3), .D_2(i4), .E(i5), .F(i6), .G(i7));
  display display_11 (
    .A(store_memory3_q2[3]), .B(store_memory3_q2[2]), .C(store_memory3_q2[1]), .D(store_memory3_q2[0]),
    .A_2(m1), .B_2(m2), .C_2(m3), .D_2(m4), .E(m5), .F(m6), .G(m7));
  display display_12 (
    .A(store_memory3_q1[3]), .B(store_memory3_q1[2]), .C(store_memory3_q1[1]), .D(store_memory3_q1[0]),
    .A_2(n1), .B_2(n2), .C_2(n3), .D_2(n4), .E(n5), .F(n6), .G(n7));
  display display_13 (
    .A(Store_memory1_q1[3]), .B(Store_memory1_q1[2]), .C(Store_memory1_q1[1]), .D(Store_memory1_q1[0]),
    .A_2(d1), .B_2(d2), .C_2(d3), .D_2(d4), .E(d5), .F(d6), .G(d7));
  display display_14 (
    .A(store_memory2_q0[3]), .B(store_memory2_q0[2]), .C(store_memory2_q0[1]), .D(store_memory2_q0[0]),
    .A_2(j1), .B_2(j2), .C_2(j3), .D_2(j4), .E(j5), .F(j6), .G(j7));
  display display_15 (
    .A(store_memory3_q0[3]), .B(store_memory3_q0[2]), .C(store_memory3_q0[1]), .D(store_memory3_q0[0]),
    .A_2(o1), .B_2(o2), .C_2(o3), .D_2(o4), .E(o5), .F(o6), .G(o7));
  _7_Segment_Display u_7_segment_display_18 ();  // open: g, f, a, b, e, d, c, dp
endmodule

// D_TO_BCD
module DCML_to_BCD (
  input  _0,
  input  _1,
  input  _2,
  input  _3,
  input  _4,
  input  _5,
  input  _6,
  input  _7,
  input  _8,
  input  _9,
  output Enable,
  output A,
  output B,
  output C,
  output D
);

  wire and_1_out, and_2_out, and_3_out, and_4_out, and_5_out, and_6_out, and_7_out, and_8_out, and_9_out;

  or or_1 (Enable, _0, _1, _2, _3, _4, _5, _6, _7, _8, _9);
  and and_1 (and_1_out, _3, Enable);
  and and_2 (and_2_out, _4, Enable);
  and and_3 (and_3_out, _5, Enable);
  and and_4 (and_4_out, _6, Enable);
  and and_5 (and_5_out, _7, Enable);
  and and_6 (and_6_out, _8, Enable);
  and and_7 (and_7_out, _9, Enable);
  and and_8 (and_8_out, _1, Enable);
  and and_9 (and_9_out, _2, Enable);
  or u_A (A, and_6_out, and_7_out);
  or u_B (B, and_5_out, and_2_out, and_3_out, and_4_out);
  or u_C (C, and_9_out, and_1_out, and_4_out, and_5_out);
  or u_D (D, and_8_out, and_1_out, and_3_out, and_5_out, and_7_out);
endmodule

// 7_segment_Input
module _7_Segment (
  input  A,
  input  B,
  input  C,
  input  D,
  input  En,
  output A_2,
  output B_2,
  output C_2,
  output D_2,
  output E,
  output F,
  output G
);

  wire B_prime_C_out, B_prime_D_prime_out, BC_prime_D_out, BC_prime_out, BD_out, BD_prime_out,
       C_prime_D_prime_out, CD_out, CD_prime_out, not_1_out, not_2_out, not_3_out, or_1_out, or_2_out,
       or_3_out, or_4_out, or_5_out, or_6_out, or_7_out;

  not not_1 (not_1_out, B);
  not not_2 (not_2_out, C);
  not not_3 (not_3_out, D);
  and CD_prime (CD_prime_out, C, not_3_out);
  and B_prime_C (B_prime_C_out, not_1_out, C);
  and BC_prime (BC_prime_out, B, not_2_out);
  and BD_prime (BD_prime_out, B, not_3_out);
  or or_1 (or_1_out, B, not_2_out, D);
  and BC_prime_D (BC_prime_D_out, D, BC_prime_out);
  and BD (BD_out, B, D);
  and B_prime_D_prime (B_prime_D_prime_out, not_1_out, not_3_out);
  and CD (CD_out, C, D);
  and C_prime_D_prime (C_prime_D_prime_out, not_2_out, not_3_out);
  or or_2 (or_2_out, CD_out, not_1_out, C_prime_D_prime_out);
  or or_3 (or_3_out, B_prime_D_prime_out, CD_prime_out, B_prime_C_out, A, BC_prime_D_out);
  or or_4 (or_4_out, C_prime_D_prime_out, BD_prime_out, BC_prime_out, A);
  or or_5 (or_5_out, CD_prime_out, BC_prime_out, A, B_prime_C_out);
  or or_6 (or_6_out, BD_out, B_prime_D_prime_out, A, C);
  or or_7 (or_7_out, CD_prime_out, B_prime_D_prime_out);
  and and_1 (A_2, or_6_out, En);
  and and_2 (B_2, or_2_out, En);
  and and_3 (C_2, En, or_1_out);
  and and_4 (D_2, or_3_out, En);
  and and_5 (E, or_7_out, En);
  and and_6 (F, or_4_out, En);
  and and_7 (G, or_5_out, En);
endmodule

module \output  (
  input  A,
  output e,
  output a_2,
  output b,
  output c,
  output d,
  output f
);

  wire not_1_out;

  not not_1 (not_1_out, A);
  or or_1 (a_2, not_1_out, A);

  assign b = a_2;
  assign c = a_2;
  assign d = a_2;
  assign e = A;
  assign f = a_2;
endmodule

module comparator (
  input  [3:0] A4,
  input  [3:0] B4,
  input  [3:0] A3,
  input  [3:0] B3,
  input  [3:0] A2,
  input  [3:0] B2,
  input  [3:0] A1,
  input  [3:0] B1,
  input  [3:0] X1,
  input  [3:0] X2,
  output \output 
);

  wire comparator_1_eq, comparator_2_eq, comparator_3_eq, comparator_4_eq, comparator_5_eq;

  Comparator #(.width(4)) comparator_1 (.a(A4), .b(B4), .eq(comparator_1_eq));  // open: gt, lt
  Comparator #(.width(4)) comparator_2 (.a(A3), .b(B3), .eq(comparator_2_eq));  // open: gt, lt
  Comparator #(.width(4)) comparator_3 (.a(A2), .b(B2), .eq(comparator_3_eq));  // open: gt, lt
  Comparator #(.width(4)) comparator_4 (.a(A1), .b(B1), .eq(comparator_4_eq));  // open: gt, lt
  Comparator #(.width(4)) comparator_5 (.a(X1), .b(X2), .eq(comparator_5_eq));  // open: gt, lt
  and and_1 (\output , comparator_1_eq, comparator_2_eq, comparator_3_eq, comparator_4_eq, comparator_5_eq);

  // Notes on the sheet:
  //   P
  //   Q
  //   R
  //   S
endmodule

module control (
  input  e,
  input  s1,
  input  s2,
  input  s3,
  output I,
  output p1,
  output p2,
  output p3
);

  wire not_1_out, not_2_out, not_3_out, not_4_out, not_5_out, not_6_out, not_7_out, not_8_out, not_9_out;

  not not_1 (not_1_out, s1);
  not not_2 (not_2_out, s3);
  not not_3 (not_3_out, s1);
  not not_4 (not_4_out, s2);
  not not_5 (not_5_out, s3);
  not not_6 (not_6_out, s2);
  not not_7 (not_7_out, s3);
  not not_8 (not_8_out, s1);
  not not_9 (not_9_out, s2);
  and and_1 (I, e, not_3_out, not_4_out, not_5_out);
  and and_2 (p1, e, s1, not_6_out, not_7_out);
  and and_3 (p2, e, not_1_out, s2, not_2_out);
  and and_4 (p3, e, not_8_out, not_9_out, s3);
endmodule

module display (
  input  A,
  input  B,
  input  C,
  input  D,
  output A_2,
  output B_2,
  output C_2,
  output D_2,
  output E,
  output F,
  output G
);

  wire B_prime_C_out, B_prime_D_prime_out, BC_prime_D_out, BC_prime_out, BD_out, BD_prime_out,
       C_prime_D_prime_out, CD_out, CD_prime_out, not_1_out, not_2_out, not_3_out;

  not not_1 (not_1_out, B);
  not not_2 (not_2_out, C);
  not not_3 (not_3_out, D);
  and CD_prime (CD_prime_out, C, not_3_out);
  and B_prime_C (B_prime_C_out, not_1_out, C);
  and BC_prime (BC_prime_out, B, not_2_out);
  and BD_prime (BD_prime_out, B, not_3_out);
  or or_1 (C_2, B, not_2_out, D);
  and BC_prime_D (BC_prime_D_out, D, BC_prime_out);
  and BD (BD_out, B, D);
  and B_prime_D_prime (B_prime_D_prime_out, not_1_out, not_3_out);
  and CD (CD_out, C, D);
  and C_prime_D_prime (C_prime_D_prime_out, not_2_out, not_3_out);
  or or_2 (B_2, CD_out, not_1_out, C_prime_D_prime_out);
  or or_3 (D_2, B_prime_D_prime_out, CD_prime_out, B_prime_C_out, A, BC_prime_D_out);
  or or_4 (F, C_prime_D_prime_out, BD_prime_out, BC_prime_out, A);
  or or_5 (G, CD_prime_out, BC_prime_out, A, B_prime_C_out);
  or or_6 (A_2, BD_out, B_prime_D_prime_out, A, C);
  or or_7 (E, CD_prime_out, B_prime_D_prime_out);
endmodule
